// Logisim project homework1.circ as structural Verilog: 9 circuits, main circuit main
module driver (
  input  [3:0] Qin,
  input  Pin,
  output a,
  output b,
  output p,
  output c,
  output d,
  output e,
  output f,
  output g
);

  wire and_1_out, and_2_out, and_3_out, and_4_out, and_5_out, and_6_out, and_7_out, and_8_out, and_9_out,
       and_10_out, and_11_out, and_12_out, and_13_out, and_14_out, and_15_out, and_16_out, not_1_out;

  and and_1 (and_1_out, ~Qin[0], ~Qin[2]);  // AND_Gate
  and and_2 (and_2_out, Qin[0], Qin[2]);
  and and_3 (and_3_out, Qin[1], Qin[0]);
  and and_4 (and_4_out, ~Qin[1], ~Qin[0]);  // AND_Gate
  and and_5 (and_5_out, ~Qin[2], ~Qin[0]);  // AND_Gate
  and and_6 (and_6_out, Qin[1], ~Qin[0]);  // AND_Gate
  and and_7 (and_7_out, ~Qin[2], Qin[1]);  // AND_Gate
  and and_8 (and_8_out, ~Qin[1], Qin[2], Qin[0]);  // AND_Gate
  and and_9 (and_9_out, ~Qin[2], ~Qin[0]);  // AND_Gate
  and and_10 (and_10_out, Qin[1], ~Qin[0]);  // AND_Gate
  and and_11 (and_11_out, ~Qin[1], ~Qin[0]);  // AND_Gate
  and and_12 (and_12_out, Qin[2], ~Qin[1]);  // AND_Gate
  and and_13 (and_13_out, Qin[2], ~Qin[0]);  // AND_Gate
  and and_14 (and_14_out, Qin[2], ~Qin[1]);  // AND_Gate
  and and_15 (and_15_out, ~Qin[2], Qin[1]);  // AND_Gate
  and and_16 (and_16_out, Qin[1], ~Qin[0]);  // AND_Gate
  or or_1 (a, and_1_out, and_2_out, Qin[1], Qin[3]);
  not not_1 (not_1_out, Qin[2]);
  or or_2 (b, not_1_out, and_3_out, and_4_out);
  or or_3 (c, Qin[2], Qin[0], ~Qin[1]);  // OR_Gate
  or or_4 (d, Qin[3], and_5_out, and_6_out, and_7_out, and_8_out);
  or or_5 (e, and_9_out, and_10_out);
  or or_6 (f, Qin[3], and_11_out, and_12_out, and_13_out);
  or or_7 (g, Qin[3], and_14_out, and_15_out, and_16_out);
  _7_Segment_Display u_7_segment_display_1 (.g(g), .f(f), .a(a), .b(b), .e(e), .d(d), .c(c), .dp(Pin));

  assign p = Pin;
endmodule

module main (
);

  wire Clk, MemLd, PCinc, PCload;
  wire [11:0] adder_1_out, AddrOut, pc_1_out_5, undriven;
  wire [15:0] Din;

  Clock clock_1 (.out(Clk));
  Adder #(.width(12)) adder_1 (.a(pc_1_out_5), .b(Din[11:0]), .out(adder_1_out));  // open: cin, cout
  PC_2 pc_1 (.Data(adder_1_out), .Load(PCload), .Clk(Clk), .Increment(PCinc), .out_5(pc_1_out_5));
  Multiplexer #(.width(12), .enable("false")) multiplexer_1 (
    .in0(pc_1_out_5), .in1(undriven), .out(AddrOut));  // open: sel
  RAM #(.addrWidth(12), .dataWidth(16)) ram_1 (
    .addr(AddrOut), .data(Din), .sel(1'b1), .clk(Clk), .ld(MemLd));  // open: clr
  register_bank register_bank_1 ();  // open: Data, Register_Select, Load, Dout1, Dout2, Dout3, Dout4, Dout5, Dout6, Dout7, Dout8, Clk

  // Other names for the same wires on the sheet: IR[11:0] = Din[11:0]; Opcode[3:0] = Din[15:12]
endmodule

module register_1 (
  input  CLK,
  input  Data,
  input  Load,
  output Q
);

  wire and_1_out, and_2_out;

  and and_1 (and_1_out, Data, Load);
  and and_2 (and_2_out, ~Data, Load);  // AND_Gate
  S_R_Flip_Flop s_r_ff_1 (.S(and_1_out), .clk(CLK), .R(and_2_out), .Q(Q), .en(1'b1));  // open: Qn, preset, reset
endmodule

module register_16 (
  input  [15:0] Data,
  input  Load,
  input  Clk,
  output [15:0] Q
);

  register_1 register_1_1 (.CLK(Clk), .Data(Data[0]), .Load(Load), .Q(Q[0]));
  register_1 register_1_2 (.CLK(Clk), .Data(Data[1]), .Load(Load), .Q(Q[1]));
  register_1 register_1_3 (.CLK(Clk), .Data(Data[2]), .Load(Load), .Q(Q[2]));
  register_1 register_1_4 (.CLK(Clk), .Data(Data[3]), .Load(Load), .Q(Q[3]));
  register_1 register_1_5 (.CLK(Clk), .Data(Data[4]), .Load(Load), .Q(Q[4]));
  register_1 register_1_6 (.CLK(Clk), .Data(Data[5]), .Load(Load), .Q(Q[5]));
  register_1 register_1_7 (.CLK(Clk), .Data(Data[6]), .Load(Load), .Q(Q[6]));
  register_1 register_1_8 (.CLK(Clk), .Data(Data[7]), .Load(Load), .Q(Q[7]));
  register_1 register_1_9 (.CLK(Clk), .Data(Data[8]), .Load(Load), .Q(Q[8]));
  register_1 register_1_10 (.CLK(Clk), .Data(Data[9]), .Load(Load), .Q(Q[9]));
  register_1 register_1_11 (.CLK(Clk), .Data(Data[10]), .Load(Load), .Q(Q[10]));
  register_1 register_1_12 (.CLK(Clk), .Data(Data[11]), .Load(Load), .Q(Q[11]));
  register_1 register_1_13 (.CLK(Clk), .Data(Data[12]), .Load(Load), .Q(Q[12]));
  register_1 register_1_14 (.CLK(Clk), .Data(Data[13]), .Load(Load), .Q(Q[13]));
  register_1 register_1_15 (.CLK(Clk), .Data(Data[14]), .Load(Load), .Q(Q[14]));
  register_1 register_1_16 (.CLK(Clk), .Data(Data[15]), .Load(Load), .Q(Q[15]));
endmodule

module register_incdec (
  input  [15:0] Data,
  input  Load,
  input  Clk,
  input  Increment,
  input  Decrement,
  output [15:0] out_6
);

  wire not_1_out, or_1_out, or_2_out;
  wire [15:0] adder_1_out, multiplexer_1_out, multiplexer_2_out, subtractor_1_out;

  or or_1 (or_1_out, Increment, Decrement);
  Multiplexer #(.width(16), .enable("false")) multiplexer_1 (
    .in0(multiplexer_2_out), .in1(Data), .out(multiplexer_1_out), .sel(not_1_out));
  not not_1 (not_1_out, or_1_out);
  or or_2 (or_2_out, Load, or_1_out);
  register_16 register_16_1 (.Data(multiplexer_1_out), .Load(or_2_out), .Q(out_6), .Clk(Clk));
  Adder #(.width(16)) adder_1 (.a(16'h1), .b(out_6), .out(adder_1_out));  // open: cin, cout
  Multiplexer #(.width(16), .enable("false")) multiplexer_2 (
    .in0(adder_1_out), .in1(subtractor_1_out), .out(multiplexer_2_out), .sel(Decrement));
  Subtractor #(.width(16)) subtractor_1 (.a(out_6), .b(16'h1), .out(subtractor_1_out));  // open: bin, bout
endmodule

module register_bank (
  input  [15:0] Data,
  input  [2:0] Register_Select,
  input  Load,
  input  Clk,
  output [15:0] Dout1,
  output [15:0] Dout2,
  output [15:0] Dout3,
  output [15:0] Dout4,
  output [15:0] Dout5,
  output [15:0] Dout6,
  output [15:0] Dout7,
  output [15:0] Dout8
);

  wire and_1_out, and_2_out, and_3_out, and_4_out, and_5_out, and_6_out, and_7_out, and_8_out,
       decoder_1_out0, decoder_1_out1, decoder_1_out2, decoder_1_out3, decoder_1_out4, decoder_1_out5,
       decoder_1_out6, decoder_1_out7;

  Decoder #(.select(3), .enable("false")) decoder_1 (
    .out0(decoder_1_out0), .out1(decoder_1_out1), .out2(decoder_1_out2), .out3(decoder_1_out3),
    .out4(decoder_1_out4), .out5(decoder_1_out5), .out6(decoder_1_out6), .out7(decoder_1_out7),
    .sel(Register_Select));
  and and_1 (and_1_out, decoder_1_out0, Load);
  and and_2 (and_2_out, decoder_1_out1, Load);
  and and_3 (and_3_out, decoder_1_out2, Load);
  and and_4 (and_4_out, decoder_1_out3, Load);
  and and_5 (and_5_out, decoder_1_out4, Load);
  and and_6 (and_6_out, decoder_1_out5, Load);
  and and_7 (and_7_out, decoder_1_out6, Load);
  and and_8 (and_8_out, decoder_1_out7, Load);
  register_16 register_16_1 (.Data(Data), .Load(and_1_out), .Q(Dout1), .Clk(Clk));
  register_16 register_16_2 (.Data(Data), .Load(and_2_out), .Q(Dout2), .Clk(Clk));
  register_16 register_16_3 (.Data(Data), .Load(and_3_out), .Q(Dout3), .Clk(Clk));
  register_16 register_16_4 (.Data(Data), .Load(and_4_out), .Q(Dout4), .Clk(Clk));
  register_16 register_16_5 (.Data(Data), .Load(and_5_out), .Q(Dout5), .Clk(Clk));
  register_16 register_16_6 (.Data(Data), .Load(and_6_out), .Q(Dout6), .Clk(Clk));
  register_16 register_16_7 (.Data(Data), .Load(and_7_out), .Q(Dout7), .Clk(Clk));
  register_16 register_16_8 (.Data(Data), .Load(and_8_out), .Q(Dout8), .Clk(Clk));
endmodule

module alu (
  input  [15:0] i1,
  input  [15:0] i2,
  input  [5:0] ALUOP,
  output [15:0] Result,
  output Zero
);

  wire [15:0] adder_1_out, adder_2_out, and_1_out, multiplexer_1_out, not_1_out, subtractor_1_out,
       subtractor_2_out, xor_1_out;

  Adder #(.width(16)) adder_1 (.a(i1), .b(i2), .out(adder_1_out));  // open: cin, cout
  Subtractor #(.width(16)) subtractor_1 (.a(i1), .b(i2), .out(subtractor_1_out));  // open: bin, bout
  assign and_1_out = i1 & i2;  // AND_Gate and_1, 16 bits wide
  assign and_1_out = i1 | i2;  // OR_Gate or_1, 16 bits wide
  assign xor_1_out = i1 ^ i2;  // XOR_Gate xor_1, 16 bits wide
  assign not_1_out = ~i1;  // NOT_Gate not_1, 16 bits wide
  Adder #(.width(16)) adder_2 (.a(i1), .b(16'h1), .out(adder_2_out));  // open: cin, cout
  Subtractor #(.width(16)) subtractor_2 (.a(i1), .b(16'h1), .out(subtractor_2_out));  // open: bin, bout
  Multiplexer #(.select(3), .width(16), .enable("false")) multiplexer_1 (
    .in0(not_1_out), .in1(i1), .in2(adder_2_out), .in3(subtractor_2_out), .out(multiplexer_1_out),
    .sel(ALUOP[2:0]));  // open: in4, in5, in6, in7
  Multiplexer #(.select(3), .width(16), .enable("false")) multiplexer_2 (
    .in0(adder_1_out), .in1(subtractor_1_out), .in2(and_1_out), .in3(and_1_out), .in4(xor_1_out),
    .in7(multiplexer_1_out), .out(Result), .sel(ALUOP[5:3]));  // open: in5, in6
  nor nor_1 (Zero, Result[15], Result[14], Result[13], Result[12], Result[11], Result[10], Result[9], Result[8], Result[7], Result[6], Result[5], Result[4], Result[3], Result[2], Result[1], Result[0]);
endmodule

module PC (
  input  [11:0] Data,
  input  Load,
  input  Clk,
  output [11:0] Q
);

  register_1 register_1_1 (.CLK(Clk), .Data(Data[0]), .Load(Load), .Q(Q[0]));
  register_1 register_1_2 (.CLK(Clk), .Data(Data[1]), .Load(Load), .Q(Q[1]));
  register_1 register_1_3 (.CLK(Clk), .Data(Data[2]), .Load(Load), .Q(Q[2]));
  register_1 register_1_4 (.CLK(Clk), .Data(Data[3]), .Load(Load), .Q(Q[3]));
  register_1 register_1_5 (.CLK(Clk), .Data(Data[4]), .Load(Load), .Q(Q[4]));
  register_1 register_1_6 (.CLK(Clk), .Data(Data[5]), .Load(Load), .Q(Q[5]));
  register_1 register_1_7 (.CLK(Clk), .Data(Data[6]), .Load(Load), .Q(Q[6]));
  register_1 register_1_8 (.CLK(Clk), .Data(Data[7]), .Load(Load), .Q(Q[7]));
  register_1 register_1_9 (.CLK(Clk), .Data(Data[8]), .Load(Load), .Q(Q[8]));
  register_1 register_1_10 (.CLK(Clk), .Data(Data[9]), .Load(Load), .Q(Q[9]));
  register_1 register_1_11 (.CLK(Clk), .Data(Data[10]), .Load(Load), .Q(Q[10]));
  register_1 register_1_12 (.CLK(Clk), .Data(Data[11]), .Load(Load), .Q(Q[11]));
endmodule

module PC_2 (
  input  [11:0] Data,
  input  Load,
  input  Clk,
  input  Increment,
  output [11:0] out_5
);

  wire not_1_out, or_1_out;
  wire [11:0] adder_1_out, multiplexer_1_out;

  Multiplexer #(.width(12), .enable("false")) multiplexer_1 (
    .in0(adder_1_out), .in1(Data), .out(multiplexer_1_out), .sel(not_1_out));
  or or_1 (or_1_out, Load, Increment);
  not not_1 (not_1_out, Increment);
  PC pc_1 (.Data(multiplexer_1_out), .Load(or_1_out), .Q(out_5), .Clk(Clk));
  Adder #(.width(12)) adder_1 (.a(12'h1), .b(out_5), .out(adder_1_out));  // open: cin, cout
endmodule
